# Fritzing sketch schematic-arduino (saved by Fritzing 0.9.4)
breadboards: 1

parts:
  Part1 = Arduino Uno (Rev3)
  LED1 = LED - 5mm [color="Red (633nm)" package="5 mm [THT]"]
  R1 = Resistor [tolerance=±5% resistance=10k package=THT]

nets:
  N1: Part1.A0, R1.Pin_0
  N2: Part1.D13/SCK, LED1.anode
  N3: Part1.GND, LED1.cathode, R1.Pin_1
